# Fritzing sketch Gesamtplatine PhysComp (saved by Fritzing 0.9.3b)
perfboards: 2

parts:
  Bauteil1 = Arduino Nano (Rev3.0)  # not connected
  R1 = Resistor [tolerance=±5% resistance=220 package="0805 [SMD]"]
  C1 = Ceramic Capacitor [capacitance=100nF package="100 mil [THT, multilayer]"]
  C3 = Capacitor Polarized [package=nippon_f80]  # not connected
  R2 = Resistor [tolerance=±5% resistance=220 package=THT]  # not connected
  C4 = Ceramic Capacitor [capacitance=100nF package="100 mil [THT, multilayer]"]
  R3 = Resistor [tolerance=±5% resistance=220 package=THT]

nets:
  N1: R1.Pin_0, C1.0
  N2: R1.Pin_1, C1.1
  N3: C4.0, R3.Pin_0
  N4: C4.1, R3.Pin_1
